// Digital circuit CORE.dig as structural Verilog
module CORE (
  input  CLK_in,
  input  nCLR,
  input  [7:0] IRQ_IN,
  input  MC,
  input  SW,
  input  Go,
  input  Stall,
  output [15:0] PC,
  output [11:0] MIPC,
  output CLK,
  output [7:0] IO_SFR,
  output [7:0] ADDR,
  output nSFR_WE,
  output nSFR_OE,
  output [7:0] nIRQ_CLRB,
  output [7:0] DBUS_inter,
  output IR_WE
);

  wire ALUD_CO, BR_CPLQ, BR_Q, CLK_aync, comparator_1_eq, comparator_1_gt, comparator_1_lt, comparator_2_eq,
       decoder_2_out_0, decoder_2_out_1, decoder_2_out_2, decoder_2_out_3, decoder_2_out_4, decoder_2_out_5,
       decoder_2_out_6, decoder_2_out_7, DPC_JUMP, IRQ_CAI, MIPC_DECVEC, nALUD_CO, nALUDH_OE, nALUDL_OE,
       nALUS_OE, nand_3_out, nDPC_JUMP, nIMMED_OE, nIRQ_OE, not_11_out, nRAM_OE, nRF_OE, nRFSRCR_WE, nROM_OE,
       nSR_WE, nWR_WE, nXRAM_OE, RAM_WE, rf_ctl_1_orf_we, RF_SFR, RF_WE, SFR_HIT, XRAM_WE;
  wire [2:0] BR_SRC, BUS_SRC, JUMP_TYPE;
  wire [3:0] ALUSD_FUNC, rf_ctl_1_orf_src, RF_SRC;
  wire [7:0] IMMED, RF_Q;
  wire [11:0] ADDRESS, multiplexer_1_out;
  wire [15:8] ADDR_16;
  wire [47:47] DECODER_d;

  BUS_TRAN bus_tran_1 (
    .SFR_HIT(SFR_HIT), .SSFR(RF_SFR), .RAM_WE(RAM_WE), .nRAM_OE(nRAM_OE), .ADDR(ADDR), .BUS_A(DBUS_inter),
    .BUS_B(IO_SFR));
  PCE PCER (.CLK(CLK), .D(DBUS_inter), .RS(RF_SRC), .WE(RF_WE), .Q(PC));
  assign DBUS_inter = ~nIRQ_OE ? IRQ_IN : 8'bz;  // DriverInvSel driverinvsel_1
  assign DBUS_inter = ~nIMMED_OE ? IMMED : 8'bz;  // DriverInvSel driverinvsel_2
  PullDown #(.Bits(8)) pulldown_1 (.out(DBUS_inter));
  assign DBUS_inter = ~nRF_OE ? RF_Q : 8'bz;  // DriverInvSel driverinvsel_3
  // Probe on DBUS_inter
  STALL u_STALL (
    .Stall(Stall), .Go(Go), .nCLR(nCLR), .SW(SW), .CLK_manual(MC), .CLK_in(CLK_in), .CLK(CLK),
    .CLK_async(CLK_aync));
  Multiplexer #(.Bits(12)) multiplexer_1 (
    .sel(MIPC_DECVEC), .in_0(ADDRESS), .in_1({3'b000, RF_Q, 1'b1}), .out(multiplexer_1_out));
  Comparator #(.Bits(8)) comparator_1 (
    .a(RF_Q), .b(IMMED), .gt(comparator_1_gt), .eq(comparator_1_eq), .lt(comparator_1_lt));
  CLRIRR clrirr_1 (.D(DBUS_inter), .IRR_CLR(IRQ_CAI), .Q(nIRQ_CLRB));
  DCOUTER #(.generic("Bits := 12;")) dcouter_1 (
    .CLK(CLK), .nCLR(nCLR), .CNT(1'b1), .nLE(nDPC_JUMP), .D(multiplexer_1_out), .Q(MIPC));
  Multiplexer #(.Selector_Bits(3)) multiplexer_2 (
    .sel(JUMP_TYPE), .in_0(1'b0), .in_1(1'b1), .in_2(comparator_1_gt), .in_3(comparator_1_eq),
    .in_4(comparator_1_lt), .in_5(BR_Q), .in_6(ALUD_CO), .in_7(nALUD_CO), .out(DPC_JUMP));
  not not_1 (nDPC_JUMP, DPC_JUMP);
  RF_CTL rf_ctl_1 (
    .CLK(CLK), .BUS_D(DBUS_inter), .RF_SRC(RF_SRC), .RF_WE(RF_WE), .RF_SFR(RF_SFR), .nRFSRCR_WE(nRFSRCR_WE),
    .nRAM_WE(RAM_WE), .nRAM_OE(nRAM_OE), .ORF_SRC(rf_ctl_1_orf_src), .ORF_WE(rf_ctl_1_orf_we),
    .nORF_OE(nRF_OE), .SFR_HIT(SFR_HIT));
  ROM #(.AddrBits(12), .Bits(48)) DECODER (
    .A(MIPC), .sel(1'b1),
    .D({DECODER_d[47], MIPC_DECVEC, JUMP_TYPE, BUS_SRC, ALUSD_FUNC, XRAM_WE, RAM_WE, nSR_WE, nWR_WE, IRQ_CAI, nRFSRCR_WE, RF_SFR, RF_WE, RF_SRC, BR_CPLQ, BR_SRC, ADDRESS, IMMED}));
  Comparator #(.Bits(4)) comparator_2 (.a(rf_ctl_1_orf_src), .b(4'b1010), .eq(comparator_2_eq));  // open: gt, lt
  nand nand_1 (nSFR_WE, RF_SFR, RAM_WE);
  nand nand_2 (nSFR_OE, RF_SFR, ~nRAM_OE);  // NAnd
  // reg_file RF: pin names not known; wires that end beside it: CLK, DBUS_inter, rf_ctl_1_orf_src, rf_ctl_1_orf_we, RF_Q
  and and_1 (IR_WE, comparator_2_eq, rf_ctl_1_orf_we);
  // Probe on MIPC
  // Probe on IMMED
  // Probe on ADDRESS
  // Probe on BR_SRC
  // Probe on BR_CPLQ
  // Probe on RF_SRC
  // Probe on RF_WE
  // Probe on RF_SFR
  // Probe on nRFSRCR_WE
  // Probe on IRQ_CAI
  // Probe on nWR_WE
  // Probe on nSR_WE
  // Probe on RAM_WE
  // Probe on XRAM_WE
  // Probe on ALUSD_FUNC
  // Probe on BUS_SRC
  // Probe on JUMP_TYPE
  // Probe on MIPC_DECVEC
  // Probe on RF_Q
  nand nand_3 (nand_3_out, CLK_aync, XRAM_WE);
  reg__sync_clear #(.generic("Bits := 8;")) WR (.D(DBUS_inter), .CLK(CLK), .CLR(nCLR), .nLE(nWR_WE), .Q(ADDR_16));
  reg__sync_clear #(.generic("Bits := 8;")) SR (.D(DBUS_inter), .CLK(CLK), .CLR(nCLR), .nLE(nSR_WE), .Q(ADDR));
  Decoder #(.Selector_Bits(3)) decoder_2 (
    .sel(BUS_SRC), .out_0(decoder_2_out_0), .out_1(decoder_2_out_1), .out_2(decoder_2_out_2),
    .out_3(decoder_2_out_3), .out_4(decoder_2_out_4), .out_5(decoder_2_out_5), .out_6(decoder_2_out_6),
    .out_7(decoder_2_out_7));
  not not_2 (nALUS_OE, decoder_2_out_0);
  not not_3 (nALUDL_OE, decoder_2_out_1);
  not not_4 (nALUDH_OE, decoder_2_out_2);
  not not_5 (nRAM_OE, decoder_2_out_3);
  not not_6 (nROM_OE, decoder_2_out_4);
  not not_7 (nXRAM_OE, decoder_2_out_5);
  not not_8 (nIMMED_OE, decoder_2_out_6);
  not not_9 (nIRQ_OE, decoder_2_out_7);
  not not_10 (nALUD_CO, ALUD_CO);
  RAMSinglePortSel #(.AddrBits(16), .isProgramMemory("true"), .Bits(8)) XRAM (
    .A({ADDR_16, ADDR}), .CS(~1'b0), .WE(~nand_3_out), .OE(~nXRAM_OE), .D(DBUS_inter));
  // Probe WRQ on ADDR_16
  // Probe SRQ on ADDR
  not not_11 (not_11_out, nROM_OE);
  ALU ALU (
    .A(RF_Q), .B(ADDR_16), .S(ALUSD_FUNC), .CI(BR_Q), .SOE(nALUS_OE), .DLOE(nALUDL_OE), .DHOE(nALUDH_OE),
    .O(DBUS_inter), .CO(ALUD_CO));
  ROM #(.AddrBits(16), .Bits(8)) ROM (.A({ADDR_16, ADDR}), .sel(not_11_out), .D(DBUS_inter));
  RAM RAM (.AC(CLK_aync), .A(ADDR), .WE(RAM_WE), .nOE(nRAM_OE), .Dt(RF_SFR), .O(DBUS_inter));
  BR BR (
    .CLK(CLK), .nCLR(nCLR), .S(BR_SRC), .I4(ALUD_CO), .I5(nALUD_CO), .I6(RF_Q[0]), .I7(RF_Q[7]),
    .CPQ(BR_CPLQ), .Q(BR_Q));

  // Other names for the same wires on the sheet: ADDR_16[7:0] = ADDR; ADDR_RAM[7:0] = ADDR; BUS_D[7:0] = DBUS_inter;
  //   BUS_SFRD[7:0] = IO_SFR

  // Notes on the sheet:
  //   PC: program counter's value
  //   MIPC: microinstruction program counter's value
  //   CLK: The CPU main clock
  //   IO_SFR: IO pin connected to peripheral SFR,
  //   It is connected to the internal IO bus 
  //   through a bus transceiver.
  //   ADDR: address used by external SFR
  //   DBUS_inter: IR load value
  //   Stall: stall CPU
  //   LS161
  //   LS151/LS251
  //   contents of DECODER (hex, n*v repeats v):
  //   80340051600,80340050700,80340050700,8034004f600,8034004f600,8034004ef00,8034004ef00,
  //   8034004ee00,8034004ee00,8034004ed00,8034004ed00,8034004e700,8034004e700,8034004e200,
  //   8034004e200,8034004e200,8034004e200,8034004de00,8034004de00,8034004de00,8034004de00,
  //   8034004de00,8034004de00,8034004de00,8034004de00,8034004de00,8034004de00,8034004de00,
  //   8034004de00,8034004de00,8034004de00,8034004de00,8034004de00,8034004d100,8034004d100,
  //   8034004fb00,8034004fb00,8034004c600,8034004c600,8034004c300,8034004c300,8034004c200,
  //   8034004c200,8034004bc00,8034004bc00,8034004b700,8034004b700,8034004b700,8034004b700,
  //   8034004b300,8034004b300,8034004b300,8034004b300,8034004b300,8034004b300,8034004b300,
  //   8034004b300,8034004b300,8034004b300,8034004b300,8034004b300,8034004b300,8034004b300,
  //   8034004b300,8034004b300,8034004a700,8034004a700,8034004f600,8034004f600,8034004a200,
  //   8034004a200,8034004a100,8034004a100,80340049a00,80340049a00,80340049000,80340049000,
  //   80340048600,80340048600,80340048600,80340048600,80340047d00,80340047d00,80340047d00,
  //   80340047d00,80340047d00,80340047d00,80340047d00,80340047d00,80340047d00,80340047d00,
  //   80340047d00,80340047d00,80340047d00,80340047d00,80340047d00,80340047d00,80340047300,
  //   80340047300,8034004fb00,8034004fb00,80340046d00,80340046d00,80340046a00,80340046a00,
  //   80340046200,80340046200,80340045700,80340045700,80340044d00,80340044d00,80340044d00,
  //   80340044d00,80340044400,80340044400,80340044400,80340044400,80340044400,80340044400,
  //   80340044400,80340044400,80340044400,80340044400,80340044400,80340044400,80340044400,
  //   80340044400,80340044400,80340044400,80340044000,80340044000,8034004f600,8034004f600,
  //   80340043b00,80340043b00,80340043200,80340043200,80340043000,80340043000,80340042c00,
  //   80340042c00,80340042700,80340042700,80340042700,80340042700,80340042300,80340042300,
  //   80340042300,80340042300,80340042300,80340042300,80340042300,80340042300,80340042300,
  //   80340042300,80340042300,80340042300,80340042300,80340042300,80340042300,80340042300,
  //   80340041f00,80340041f00,8034004fb00,8034004fb00,80340041a00,80340041a00,80340041100,
  //   80340041100,80340040f00,80340040f00,80340040b00,80340040b00,80340040600,80340040600,
  //   80340040600,80340040600,80340040200,80340040200,80340040200,80340040200,80340040200,
  //   80340040200,80340040200,80340040200,80340040200,80340040200,80340040200,80340040200,
  //   80340040200,80340040200,80340040200,80340040200,8034003fe00,8034003fe00,8034004f600,
  //   8034004f600,8034003f900,8034003f900,8034003f000,8034003f000,8034003ee00,8034003ee00,
  //   8034003ea00,8034003ea00,8034003e500,8034003e500,8034003e500,8034003e500,8034003e100,
  //   8034003e100,8034003e100,8034003e100,8034003e100,8034003e100,8034003e100,8034003e100,
  //   8034003e100,8034003e100,8034003e100,8034003e100,8034003e100,8034003e100,8034003e100,
  //   8034003e100,8034003dd00,8034003dd00,8034004fb00,8034004fb00,8034003d200,8034003d200,
  //   8034003cd00,8034003cd00,8034003cc00,8034003cc00,8034003c500,8034003c500,8034003c000,
  //   8034003c000,8034003c000,8034003c000,8034003bc00,8034003bc00,8034003bc00,8034003bc00,
  //   8034003bc00,8034003bc00,8034003bc00,8034003bc00,8034003bc00,8034003bc00,8034003bc00,
  //   8034003bc00,8034003bc00,8034003bc00,8034003bc00,8034003bc00,8034003b700,8034003b700,
  //   8034004f600,8034004f600,8034003ac00,8034003ac00,8034003a800,8034003a800,80340037400,
  //   80340037400,80340036a00,80340036a00,80340036000,80340036000,80340036000,80340036000,
  //   80340035900,80340035900,80340035900,80340035900,80340035900,80340035900,80340035900,
  //   80340035900,80340035900,80340035900,80340035900,80340035900,80340035900,80340035900,
  //   80340035900,80340035900,80340035500,80340035500,8034004fb00,8034004fb00,80340034a00,
  //   80340034a00,80340034600,80340034600,80340033e00,80340033e00,80340033300,80340033300,
  //   80340032900,80340032900,80340032900,80340032900,80340032000,80340032000,80340032000,
  //   80340032000,80340032000,80340032000,80340032000,80340032000,80340032000,80340032000,
  //   80340032000,80340032000,80340032000,80340032000,80340032000,80340032000,80340031400,
  //   80340031400,8034004f600,8034004f600,80340030a00,80340030a00,80340030800,80340030800,
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  //   LS137/LS138
  //   at28c64
  //   core is at28c64
  //   contents of ROM (hex, n*v repeats v):
  //   2,c,3d,2,e,5a,30,99,fd,c2,99,8f,99,22,0,0,0,0,0,2,d,e7,2,3,27,e8,64,80,f8,e9,33,e8,
  //   33,60,11,4,60,f0,ed,33,ec,33,70,9,e8,fc,e9,fd,ea,fe,eb,ff,22,4,60,de,d3,eb,9f,ea,
  //   9e,e9,9d,e8,c2,e7,8c,f0,c2,f7,95,f0,40,c,e8,cc,f8,e9,cd,f9,ea,ce,fa,eb,cf,fb,12,2,
  //   f2,85,d0,f0,58,4,70,3,20,d5,b3,e8,4,70,7,50,2,b2,d5,2,3,31,92,d5,ec,4,60,f7,e4,cc,
  //   c0,e0,c3,98,f8,60,3b,94,18,60,8,40,d,d0,e0,fb,2,3,9,e4,fb,fa,c9,fc,80,28,e8,30,e4,
  //   6,e4,c9,fb,e4,ca,fc,e8,30,e3,5,e4,c9,ca,cb,fc,e8,54,7,60,10,f8,c3,e9,13,f9,ea,13,
  //   fa,eb,13,fb,ec,13,fc,d8,f1,30,f5,2f,c3,e4,9c,fc,ef,9b,ff,ee,9a,fe,ed,99,fd,d0,e0,
  //   fb,ef,4e,4d,4c,70,12,22,db,3,2,3,2e,ec,2c,fc,ef,33,ff,ee,33,fe,ed,33,fd,ed,30,e7,
  //   eb,2,3,9,ef,2b,ff,ee,3a,fe,ed,39,fd,d0,e0,fb,50,13,b,bb,0,3,2,3,31,ed,13,fd,ee,13,
  //   fe,ef,13,ff,ec,13,fc,2,3,9,ec,4d,60,11,e8,49,70,17,ed,33,ec,33,4,60,d,e4,fc,ff,fe,
  //   fd,22,e9,33,e8,33,4,70,f8,2,3,27,12,2,f2,58,4,60,9,e4,cc,24,81,50,6,28,50,9,2,3,31,
  //   28,40,3,2,3,2e,c0,e0,eb,4a,70,44,b9,80,6,d0,e0,fb,2,3,1d,ef,4e,70,1c,bd,80,8,eb,ff,
  //   ea,fe,e9,fd,80,eb,e9,8d,f0,a4,fe,e5,f0,2,1,f7,e9,cd,f9,ea,fe,eb,ff,ef,89,f0,a4,fc,
  //   e5,f0,ce,89,f0,a4,2e,ff,e4,35,f0,cd,89,f0,a4,2d,fe,e4,35,f0,80,67,ef,4e,70,5,bd,80,
  //   d7,80,c3,ef,8b,f0,a4,ac,f0,ee,8b,f0,a4,2c,fc,e4,35,f0,f8,ef,8a,f0,a4,2c,e5,f0,38,
  //   fc,e4,33,cb,8d,f0,a4,2c,fc,e5,f0,3b,f8,ee,8a,f0,a4,2c,fc,e5,f0,38,f8,e4,33,cf,89,
  //   f0,a4,2c,fc,e5,f0,38,cf,34,0,ce,89,f0,a4,2f,ff,e5,f0,3e,fe,e4,33,c9,8d,f0,a4,2e,fe,
  //   e5,f0,39,cd,8a,f0,a4,2f,ff,e5,f0,3e,fe,e4,3d,fd,33,d0,e0,fb,50,7,b,bb,0,f,2,3,31,
  //   ec,2c,fc,ef,33,ff,ee,33,fe,ed,33,fd,2,3,9,2,3,31,ec,5d,4,60,5,e8,59,4,70,3,2,3,27,
  //   12,2,f2,58,4,60,f6,ec,48,60,f2,ec,70,4,fd,fe,ff,22,c8,60,db,24,81,c8,50,9,c3,98,60,
  //   2,50,6,2,3,2e,98,50,ca,f5,82,e9,29,4b,4a,70,5,ab,82,2,3,1d,75,f0,0,7c,1a,78,80,c3,
  //   ef,9b,ee,9a,ed,99,40,d,c3,ef,9b,ff,ee,9a,fe,ed,99,fd,e8,42,f0,dc,23,ac,f0,d0,e0,ff,
  //   d0,e0,fe,d0,e0,fd,ab,82,20,e7,10,1b,eb,60,ba,ec,2c,fc,ef,33,ff,ee,33,fe,ed,33,fd,
  //   2,3,9,e8,3,f8,30,e7,5,c0,f0,75,f0,0,ef,2f,ff,ee,33,fe,ed,33,fd,40,b8,30,e7,c2,80,
  //   aa,75,f0,20,80,e,75,f0,10,80,5,75,f0,8,7d,0,7e,0,7f,0,33,92,d5,30,d5,3,12,6,21,ec,
  //   33,40,10,ef,33,ff,ee,33,fe,ed,33,fd,ec,33,fc,d5,f0,ed,22,e5,f0,24,7e,a2,d5,13,cc,
  //   92,e7,cd,ce,ff,22,e9,d2,e7,c9,33,e8,33,f8,92,d5,ed,d2,e7,cd,33,ec,33,fc,50,2,b2,d5,
  //   22,ec,30,e7,10,f,bf,0,c,e,be,0,8,d,bd,0,4,b,eb,60,14,a2,d5,eb,13,fc,ed,92,e7,fd,22,
  //   74,ff,fc,fd,fe,ff,22,e4,80,f8,a2,d5,74,ff,13,fc,7d,80,e4,80,ef,f9,20,e7,28,24,f9,
  //   50,3,79,7,e4,f4,24,2,fb,18,db,fd,e6,24,fb,50,14,e9,60,d,e4,f6,18,e6,4,f6,b4,a,8,e4,
  //   f6,d9,f5,74,1,f6,a,22,c2,d5,22,ed,33,ec,33,92,d5,fa,60,2a,b4,ff,33,ed,c2,e7,7b,ff,
  //   60,6,7a,3,79,90,e4,22,7a,3,79,99,20,d5,4,7a,3,79,94,22,4e,61,4e,0,2b,49,4e,46,0,2d,
  //   49,4e,46,0,e4,7a,8,f6,8,da,fc,7b,0,74,7,22,e8,c0,e0,ec,c0,e0,ed,c0,e0,ee,c0,e0,ef,
  //   c0,e0,ea,75,f0,10,a4,ca,ab,f0,75,f0,4d,a4,2b,fb,e4,35,f0,fc,ea,24,10,fa,eb,34,c5,
  //   fb,ec,34,d9,fc,ed,c2,e7,ff,75,f0,56,a4,f4,24,11,c5,f0,f4,34,c5,8f,f0,a4,2a,e5,f0,
  //   3b,e4,3c,f6,20,e7,14,12,4,9e,d0,e0,ff,d0,e0,fe,d0,e0,fd,d0,e0,fc,12,2,17,80,14,f4,
  //   4,12,4,9e,d0,e0,ff,d0,e0,fe,d0,e0,fd,d0,e0,fc,12,1,e,d0,e0,f8,e6,fa,ed,d2,e7,cd,33,
  //   ec,33,24,82,fb,e4,c3,cf,33,cf,ce,33,ce,cd,33,cd,33,db,f3,7b,7,75,f0,a,84,60,4,f6,
  //   8,1b,a,e5,f0,f6,8,8f,f0,74,a,a4,ff,ac,f0,8e,f0,74,a,a4,2c,fe,ac,f0,50,1,c,8d,f0,74,
  //   a,a4,2c,fd,e4,35,f0,f6,8,db,de,74,7,22,3f,80,0,0,41,20,0,0,42,c8,0,0,44,7a,0,0,46,
  //   1c,40,0,47,c3,50,0,49,74,24,0,4b,18,96,80,4c,be,bc,20,5a,e,1b,ca,67,53,c2,1c,74,9d,
  //   c5,ae,fb,60,6,54,7,60,1c,23,23,12,4,cc,eb,54,38,60,9,12,4,b8,12,4,c7,12,1,e,ec,f8,
  //   ed,f9,ee,fa,ef,cb,22,eb,12,4,c7,80,f1,54,38,3,24,1c,90,4,6e,fe,93,fc,e,ee,93,fd,e,
  //   ee,93,e,ce,93,ff,22,bb,1,6,89,82,8a,83,e0,22,50,2,e7,22,bb,fe,2,e3,22,89,82,8a,83,
  //   e4,93,22,bb,1,c,e5,82,29,f5,82,e5,83,3a,f5,83,e0,22,50,6,e9,25,82,f8,e6,22,bb,fe,
  //   6,e9,25,82,f8,e2,22,e5,82,29,f5,82,e5,83,3a,f5,83,e4,93,22,bb,1,6,89,82,8a,83,f0,
  //   22,50,2,f7,22,bb,fe,1,f3,22,ef,8d,f0,a4,a8,f0,cf,8c,f0,a4,28,ce,8d,f0,a4,2e,fe,22,
  //   bc,0,b,be,0,29,ef,8d,f0,84,ff,ad,f0,22,e4,cc,f8,75,f0,8,ef,2f,ff,ee,33,fe,ec,33,fc,
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  //   core is 6116
  //   L74+LS252
endmodule
